# Fritzing sketch motorController (saved by Fritzing 0.9.3b)
breadboards: 1

parts:
  U1 = LIPO-2000mAh [package=lipo-2000]
  Bauteil1 = Arduino Nano (Rev3.0)
  S1 = H-Bridge with L298N
  M1 = DC Motor  # not connected
  M2 = DC Motor

nets:
  N1: U1.+, S1.12V
  GND: U1.-, Bauteil1.GND, S1.GND
  VIN: Bauteil1.VIN, S1.5V
  N2: S1.M1-01, M2.pin_2

custom parts:
  H-Bridge with L298N: h-bridge
