# Fritzing sketch verkabelung (saved by Fritzing 0.9.3b)

parts:
  Bauteil1 = Arduino Mega 2560 (Rev3)
  S1 = H-Bridge with L298N
  M1 = DC Motor
  M2 = DC Motor
  M3 = DC Motor
  M4 = DC Motor
  U1 = LIPO-2000mAh [package=lipo-2000]
  U2 = LIPO-1000mAh [package=lipo-1000]

nets:
  5V: Bauteil1.5V, S1.5V
  GND: Bauteil1.GND, S1.GND, U1.+, U2.+
  N1: Bauteil1.VIN, U2.-
  N2: Bauteil1.D23, S1.IN1
  N3: Bauteil1.D25, S1.IN2
  N4: Bauteil1.D27, S1.IN3
  N5: Bauteil1.D29, S1.IN4
  N6: S1.12V, U1.-
  N7: S1.ENA, S1.ENA-5V
  N8: S1.ENB, S1.ENB-5V
  N9: S1.M1-01, M1.pin_2, M2.pin_2
  N10: S1.M1-02, M1.pin_1, M2.pin_1
  N11: S1.M2-01, M3.pin_2, M4.pin_2
  N12: S1.M2-02, M3.pin_1, M4.pin_1

custom parts:
  H-Bridge with L298N: h-bridge
